// Logisim project reg_file.circ as structural Verilog: 1 circuit, main circuit REG_File
module REG_File (
  input  [3:0] Reg_Sel_A,
  input  Write_Enable,
  input  [3:0] Write_Reg,
  input  [15:0] Write_Data,
  input  [3:0] Reg_Sel_B,
  input  CLK,
  input  Reset,
  output [15:0] A,
  output [15:0] B
);

  wire we_R0, we_R1, we_R2, we_R3, we_R4, we_R5, we_R6, we_R7, we_R8, we_R9, we_R10, we_R11, we_R12, we_R13,
       we_R14, we_R15;
  wire [15:0] R0_q, R1_q, R2_q, R3_q, R4_q, R5_q, R6_q, R7_q, R8_q, R9_q, R10_q, R11_q, R12_q, R13_q, R14_q,
       R15_q;

  Decoder #(.select(4)) decoder_1 (
    .out0(we_R0), .out1(we_R1), .out2(we_R2), .out3(we_R3), .out4(we_R4), .out5(we_R5), .out6(we_R6),
    .out7(we_R7), .out8(we_R8), .out9(we_R9), .out10(we_R10), .out11(we_R11), .out12(we_R12), .out13(we_R13),
    .out14(we_R14), .out15(we_R15), .sel(Write_Reg), .en(Write_Enable));
  Register #(.width(16)) R0 (.D({16{1'b0}}), .en(we_R0), .Q(R0_q));  // open: clk, clr
  Register #(.width(16)) R1 (.D(Write_Data), .en(we_R1), .clk(CLK), .Q(R1_q), .clr(Reset));
  Register #(.width(16)) R2 (.D(Write_Data), .en(we_R2), .clk(CLK), .Q(R2_q), .clr(Reset));
  Register #(.width(16)) R3 (.D(Write_Data), .en(we_R3), .clk(CLK), .Q(R3_q), .clr(Reset));
  Register #(.width(16)) R4 (.D(Write_Data), .en(we_R4), .clk(CLK), .Q(R4_q), .clr(Reset));
  Register #(.width(16)) R5 (.D(Write_Data), .en(we_R5), .clk(CLK), .Q(R5_q), .clr(Reset));
  Register #(.width(16)) R6 (.D(Write_Data), .en(we_R6), .clk(CLK), .Q(R6_q), .clr(Reset));
  Register #(.width(16)) R7 (.D(Write_Data), .en(we_R7), .clk(CLK), .Q(R7_q), .clr(Reset));
  Register #(.width(16)) R8 (.D(Write_Data), .en(we_R8), .clk(CLK), .Q(R8_q), .clr(Reset));
  Register #(.width(16)) R9 (.D(Write_Data), .en(we_R9), .clk(CLK), .Q(R9_q), .clr(Reset));
  Register #(.width(16)) R10 (.D(Write_Data), .en(we_R10), .clk(CLK), .Q(R10_q), .clr(Reset));
  Register #(.width(16)) R11 (.D(Write_Data), .en(we_R11), .clk(CLK), .Q(R11_q));  // open: clr
  Register #(.width(16)) R12 (.D(Write_Data), .en(we_R12), .clk(CLK), .Q(R12_q), .clr(Reset));
  Register #(.width(16)) R13 (.D(Write_Data), .en(we_R13), .clk(CLK), .Q(R13_q), .clr(Reset));
  Register #(.width(16)) R14 (.D(Write_Data), .en(we_R14), .clk(CLK), .Q(R14_q), .clr(Reset));
  Register #(.width(16)) R15 (.D(Write_Data), .en(we_R15), .clk(CLK), .Q(R15_q), .clr(Reset));
  Multiplexer #(.select(4), .width(16)) multiplexer_1 (
    .in0(R0_q), .in1(R1_q), .in2(R2_q), .in3(R3_q), .in4(R4_q), .in5(R5_q), .in6(R6_q), .in7(R7_q),
    .in8(R8_q), .in9(R9_q), .in10(R10_q), .in11(R11_q), .in12(R12_q), .in13(R13_q), .in14(R14_q),
    .in15(R15_q), .out(A), .sel(Reg_Sel_A));
  Multiplexer #(.select(4), .width(16)) multiplexer_2 (
    .in0(R0_q), .in1(R1_q), .in2(R2_q), .in3(R3_q), .in4(R4_q), .in5(R5_q), .in6(R6_q), .in7(R7_q),
    .in8(R8_q), .in9(R9_q), .in10(R10_q), .in11(R11_q), .in12(R12_q), .in13(R13_q), .in14(R14_q),
    .in15(R15_q), .out(B), .sel(Reg_Sel_B));

  // Notes on the sheet:
  //   MUX_A
  //   MUX_B
endmodule
